# Fritzing sketch arabaaaa (saved by Fritzing 0.9.9b)

parts:
  M1 = Getriebemotor
  M2 = Getriebemotor
  M3 = Getriebemotor
  M4 = Getriebemotor
  L298N1 = L298N DC motor driver
  Parça1 = Arduino Uno (Rev3) - ICSP
  BT1 = Bluetooth HC-06u [package=THT]
  VCC1 = Battery
  Mod1 = 2S-BMS
  TP1 = TP4056 [chip_label=TP4056 package="DIP (Dual Inline) [THT]"]
  C1 = Capacitor Polarized [package=nippon_f80]
  Solar_Cell1 = 5V 100mA Polycrystalline PET Solar Cell [part_number=IM130407002]
  S1 = Toggle Switch spst [package=THT]
  Parça2 = Arduino Nano (Rev3.0) (ICSP)
  BAT2 = Battery Holders [package=battcom_20mm_pth]
  C2 = Ceramic Capacitor [capacitance=100nF package="100 mil [THT, multilayer]"]
  R2 = Resistor [tolerance=±5% resistance=220 package="0402 [SMD]"]
  LED1 = smd LED [color="Red (633nm)" package="0805 [SMD]"]
  R3 = Resistor [tolerance=±5% resistance=220 package="0402 [SMD]"]
  D1 = Rectifier Diode [package="Melf DO-213 AA [SMD]"]
  J1 = Piezo Speaker
  R4 = Photocell (LDR) [package=THT]

nets:
  N1: M1.pin_1, M3.pin_2, L298N1.OUT3
  N2: M1.pin_2, M3.pin_1, L298N1.OUT4
  N3: M2.pin_1, M4.pin_2, L298N1.OUT1
  N4: M2.pin_2, M4.pin_1, L298N1.OUT2
  N5: L298N1.12V, S1.COM
  GND: L298N1.GND, Parça1.GND, BT1.GND, Mod1.pin3#2, TP1.pin5, Parça2.GND, BAT2.-, C2.0, LED1.cathode, J1.pin1, R4.pin_0
  5V: L298N1.5V, Parça1.VIN
  N6: L298N1.ENA, Parça1.D11_PWM/MOSI
  N7: L298N1.ENB, Parça1.D6_PWM
  N8: L298N1.IN1, Parça1.D10_PWM/SS
  N9: L298N1.IN2, Parça1.D9_PWM
  N10: L298N1.IN3, Parça1.D8
  N11: L298N1.IN4, Parça1.D7
  N12: Parça1.A0, Parça2.D2
  N13: Parça1.A3, R4.pin_1
  N14: Parça1.D0/RX, BT1.TXD
  N15: Parça1.D1/TX, BT1.RXD
  5V_2: Parça1.5V, BT1.VCC, Parça2.VIN
  N16: VCC1.-, Mod1.pin2
  N17: VCC1.+, Mod1.pin1
  N18: Mod1.pin3#3, TP1.pin4, S1.L1
  N19: TP1.pin1, C1.+, Solar_Cell1.5V
  N20: TP1.pin2, C1.-, Solar_Cell1.GND
  N21: Parça2.A3, J1.pin2
  N22: Parça2.A2, R2.Pin_0
  N23: Parça2.A0, R3.Pin_0
  N24: BAT2.+, R3.Pin_1, D1.anode

notes:
  20 Tur Bobin Sarımı

custom parts:
  L298N DC motor driver: 2x DC motor driver with 78M05 positive voltage regulator (7..35 V) L298N: max 46 V, 2 A Set 5 V Enable jumper to enable 5 V regultor (needed for the L298N) and +5 V output at screw terminal or supply external +5 V at screw terminal Set ENA and/or ENB to +5 V to enable motor permanently or supply ENA and/or ENB with PWM signal IN1 and IN2 set rotation directory for motor A (OUT1/OUT2) IN2 and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
  Bluetooth HC-06u: Bluetooth HC-06 - face up, pins down 16.5mm x 37.5mm PCB
  Battery: Your standard 2x 18650 battery pack (7.4 Volts)
  2S-BMS: 2S-BMS LIPO battery charger / protection unit. Note pcb does not match the board as it will likely connect with wires, so pcb is 5 pads suitable for .1in header pins.
  TP4056: A DIP stand-in part for whatever IC you want. With 6 pins on a 300mil dual inline package (DIP) footprint.
  5V 100mA Polycrystalline PET Solar Cell: This is 5V 100mA Polycrystalline PET Solar Cell. It is high quality and exquisite appearance. It is used in all kinds of high-grade electronic products.
  Toggle Switch spst: Toggle Switch single pole single throw
